# Fritzing sketch gy+servo (saved by Fritzing 0.9.3b)
breadboards: 2

parts:
  GY1 = MPU-6050 Board GY-521 [form="♀ (female)" package=THT]
  Componente1 = Arduino Uno (Rev3)
  J1 = Basic Servo

nets:
  5V: GY1.pin1, Componente1.5V, J1.vcc
  GND: GY1.pin2, Componente1.GND, J1.gnd
  N1: GY1.pin3, Componente1.A5/SCL
  N2: GY1.pin4, Componente1.A4/SDA
  N3: Componente1.D9_PWM, J1.pulse

custom parts:
  MPU-6050 Board GY-521: Acelerometro y Giroscopio MPU-6050 Board GY-521
