# Fritzing sketch arduinoreceive (saved by Fritzing 0.9.3b)
breadboards: 1

parts:
  Componente2 = Arduino Uno (Rev3)
  Componente3 = NRF24L01+ Breakout Board
  Componente4 = Logic Level Converter
  BT1 = Bluetooth HC-06u [package=THT]
  J1 = Basic Servo
  J2 = Basic Servo

nets:
  N1: Componente2.D8, Componente3.CS
  N2: Componente2.D9_PWM, J2.pulse
  N3: Componente2.D11_PWM/MOSI, Componente3.MOSI
  N4: Componente2.D12/MISO, Componente3.MISO
  N5: Componente2.D13/SCK, Componente3.SCK
  GND: Componente2.GND, Componente3.GND, Componente4.GND, BT1.GND, J1.gnd, J2.gnd
  N6: Componente2.D0/RX, Componente4.RX_HV
  N7: Componente2.D1/TX, Componente4.TX_HV
  N8: Componente2.D3_PWM, J1.pulse
  N9: Componente2.D7, Componente3.CE
  3V3: Componente2.3V3, Componente3.VCC, Componente4.LV
  VCC: Componente2.5V, J1.vcc, J2.vcc
  N10: Componente4.RX_LV, BT1.RXD
  N11: Componente4.TX_LV, BT1.TXD

custom parts:
  Bluetooth HC-06u: Bluetooth HC-06 - face up, pins down 16.5mm x 37.5mm PCB
