# Fritzing sketch sensori-prova-circuit (saved by Fritzing 0.8.7b)
breadboards: 1

parts:
  GY1 = MPU-6050 Board GY-521 [form="♀ (female)" package=THT]
  Componente1 = Arduino Uno (Rev3)
  J1 = Basic Servo
  Servo_clamp = Basic Servo
  DS2 = DS18B20 1-Wire Temperature Sensor Probe Cable
  R2 = Resistor [tolerance=±5% resistance=4.7k package="1206 [SMD]"]
  VCC1 = Battery block 9V
  VCC2 = Battery block 9V
  Componente2 = JeePlug experimenter's board  # not connected

nets:
  VCC: GY1.pin1, Componente1.5V, J1.vcc, Servo_clamp.vcc, DS2.VDD, R2.Pin_1
  GND: GY1.pin2, Componente1.GND, J1.gnd, Servo_clamp.gnd, DS2.GND
  N1: GY1.pin3, Componente1.A5/SCL
  N2: GY1.pin4, Componente1.A4/SDA
  N3: Componente1.D8, DS2.shield, R2.Pin_0
  N4: Componente1.D9_PWM, J1.pulse
  N5: Componente1.D6_PWM, Servo_clamp.pulse
  N6: VCC1.-, VCC2.+

custom parts:
  MPU-6050 Board GY-521: Acelerometro y Giroscopio MPU-6050 Board GY-521
